// Digital circuit max2-sketch.dig as structural Verilog
module max2_sketch (
  input  a1,
  input  a0,
  input  b1,
  input  b0,
  output r1
);

  // And and_1 has open pins: In_1=a1, In_2=a0, In_3=b1, In_4=b0, out=open
  // And and_2 is placed but not wired
  // Or or_1 has open pins: In_1=open, In_2=open, In_3=open, In_4=open, In_5=open, In_6=open, In_7=open, In_8=open, In_9=open, In_10=open, In_11=open, In_12=open, out=r1
endmodule
