// Digital circuit or-demo.dig as structural Verilog
module or_demo (
  input  a,
  input  b,
  output r
);

  wire and_1_out, and_2_out, and_3_out;

  and and_1 (and_1_out, ~a, b);  // And
  and and_2 (and_2_out, a, ~b);  // And
  and and_3 (and_3_out, a, b);
  or or_1 (r, and_1_out, and_2_out, and_3_out);
endmodule
