// Digital circuit subcircuit-demo.dig as structural Verilog
module subcircuit_demo (
);

  wire _1_bit_half_adder_1_p1, _1_bit_half_adder_2_p1;

  // _1_bit_half_adder _1_bit_half_adder_1: pin names not known; wires that end beside it: _1_bit_half_adder_1_p1
  // _1_bit_half_adder _1_bit_half_adder_2: pin names not known; wires that end beside it: _1_bit_half_adder_2_p1
endmodule
