// Digital circuit 1bha.dig as structural Verilog
module _1bha (
  input  a,
  input  b,
  output s,
  output cout
);

  wire and_1_out, and_2_out;

  and and_1 (and_1_out, ~a, b);  // And
  and and_2 (and_2_out, a, ~b);  // And
  and and_3 (cout, a, b);
  or or_1 (s, and_1_out, and_2_out);
endmodule
