// Digital circuit demo.dig as structural Verilog
module demo (
  input  [3:0] a,
  output [3:0] s
);

  _1bha _1bha_1 (.a(a[0]), .s(s[0]));  // open: b, cout
  _1bha _1bha_2 (.a(a[1]), .s(s[1]));  // open: b, cout
endmodule
