// Digital circuit d_latch.dig as structural Verilog
module d_latch (
  input  CLK,
  input  D,
  output Q,
  output notQ
);

  wire and_1_out, and_2_out;

  and and_1 (and_1_out, CLK, ~D);  // And
  and and_2 (and_2_out, CLK, D);
  sr_latch sr_latch_1 (.R(and_1_out), .S(and_2_out), .Q(Q), .notQ(notQ));
endmodule
