// Digital circuit muxdemo.dig as structural Verilog
module muxdemo (
  input  in_1,
  input  [1:0] in_3,
  output [1:0] out_2,
  output [1:0] out_4
);

  Multiplexer #(.Bits(2)) multiplexer_1 (.sel(in_1), .in_0(2'b01), .in_1(2'b10), .out(out_2));
  Multiplexer #(.Selector_Bits(2), .Bits(2)) multiplexer_2 (
    .sel(in_3), .in_0(2'b01), .in_1(2'b00), .in_2(2'b10), .in_3(2'b11), .out(out_4));
endmodule
