// Digital circuit romdemo.dig as structural Verilog
module romdemo (
  input  [7:0] A,
  output [31:0] IW
);

  ROM #(.AddrBits(8), .Bits(32)) rom_1 (.A(A), .sel(1'b1), .D(IW));

  // Notes on the sheet:
  //   contents of rom_1 (hex, n*v repeats v):
  //   100293,a2c463,8067,fe810113,113023,a13423,fff50513,fe5ff0ef,a13823
  //   ,813503,ffe50513,fd5ff0ef,1013303,650533,13083,1810113,8067,c0001073
endmodule
