// Digital circuit 4_bit_reg.dig as structural Verilog
module _4_bit_reg (
  input  [3:0] D,
  input  EN,
  input  C,
  input  CLR,
  output [3:0] Q
);

  d_flip_flop d_flip_flop_1 (.EN(EN), .C(C), .D(D[0]), .CLR(CLR), .Q(Q[0]));
  d_flip_flop d_flip_flop_2 (.EN(EN), .C(C), .D(D[1]), .CLR(CLR), .Q(Q[1]));
  d_flip_flop d_flip_flop_3 (.EN(EN), .C(C), .D(D[2]), .CLR(CLR), .Q(Q[2]));
  d_flip_flop d_flip_flop_4 (.EN(EN), .C(C), .D(D[3]), .CLR(CLR), .Q(Q[3]));
endmodule
