// Digital circuit d_flip_flop.dig as structural Verilog
module d_flip_flop (
  input  EN,
  input  C,
  input  D,
  input  CLR,
  output Q
);

  wire d_latch_1_q, multiplexer_1_out, not_1_out;

  Multiplexer multiplexer_1 (.sel(EN), .in_0(d_latch_1_q), .in_1(D), .out(multiplexer_1_out));
  not not_1 (not_1_out, C);
  d_latch d_latch_1 (.C(not_1_out), .D(multiplexer_1_out), .CLR(CLR), .Q(d_latch_1_q));  // open: notQ
  d_latch d_latch_2 (.C(C), .D(d_latch_1_q), .CLR(CLR), .Q(Q));  // open: notQ
endmodule
