// Digital circuit fun-with-mul.dig as structural Verilog
module fun_with_mul (
  input  [63:0] A,
  input  [63:0] B,
  output [63:0] R,
  output [63:0] R_2,
  output [63:0] out_5
);

  wire [63:32] mul_1_mul, mul_2_mul;

  Mul #(.Bits(32)) mul_1 (.a(A[31:0]), .b(B[31:0]), .mul({mul_1_mul, R[31:0]}));
  Mul #(.Bits(32)) mul_2 (.a(A[63:32]), .b(B[63:32]), .mul({mul_2_mul, R[63:32]}));
  Mul #(.Bits(32)) mul_3 (.a(A[31:0]), .b(B[31:0]), .mul(R_2));
  BarrelShifter #(.Bits(64)) barrelshifter_1 (.in(A), .shift(B[6:0]), .out(out_5));
endmodule
